// Logisim project logisim-adapted-timer.circ as structural Verilog
module main (
  input  in_1,
  output [7:0] out_2
);

  wire alarma_1_alarm_buzz, alarma_1_alarm_sound, alarma_1_load_register, bigcnt_1_alarmoutput, clock_1_out,
       commandunit_1_en_alarm_up, commandunit_1_enable_bigcnt, commandunit_1_set_led,
       commandunit_1_working_timer, M_out, OK_BUT_out, or_1_out, S_out, SET_ALARM_BUTT_out, START_BUT_out;
  wire [3:0] binary_to_decimal_converter_1_decimal, binary_to_decimal_converter_1_unit,
       binary_to_decimal_converter_2_decimal, binary_to_decimal_converter_2_unit,
       binary_to_decimal_converter_3_decimal, binary_to_decimal_converter_3_unit;
  wire [6:0] bcd_1_segment, bcd_2_segment, bcd_3_segment, bcd_4_segment, bcd_5_segment, bcd_6_segment;
  wire [7:0] alarma_1_counter_output, bigcnt_1_min_output, bigcnt_1_sec_output;

  Clock clock_1 (.out(clock_1_out));
  Button OK_BUT (.out(OK_BUT_out));
  Button START_BUT (.out(START_BUT_out));
  Button SET_ALARM_BUTT (.out(SET_ALARM_BUTT_out));
  Button S (.out(S_out));
  Button M (.out(M_out));
  CommandUnit commandunit_1 (
    .OK_BUT(OK_BUT_out), .clk(clock_1_out), .START_BUT(START_BUT_out),
    .alarm_input_over(alarma_1_alarm_buzz), .reset(in_1), .EN_ALARM_UP(commandunit_1_en_alarm_up),
    .SET_LED(commandunit_1_set_led), .WORKING_TIMER(commandunit_1_working_timer),
    .ENABLE_BIGCNT(commandunit_1_enable_bigcnt));
  or or_1 (or_1_out, SET_ALARM_BUTT_out, bigcnt_1_alarmoutput);
  LED SET_LED (.in(commandunit_1_set_led));
  LED TIMER_WORKING (.in(commandunit_1_working_timer));
  alarma alarma_1 (
    .reload_register(out_2), .clock(clock_1_out), .button(or_1_out), .set_alarm(commandunit_1_en_alarm_up),
    .reset(in_1), .counter_output(alarma_1_counter_output), .alarm_buzz(alarma_1_alarm_buzz),
    .alarm_sound(alarma_1_alarm_sound), .load_register(alarma_1_load_register));
  BIGCNT bigcnt_1 (
    .CLK(clock_1_out), .But(OK_BUT_out), .S(S_out), .M(M_out), .RES(in_1), .EN(commandunit_1_enable_bigcnt),
    .ALARMOUTPUT(bigcnt_1_alarmoutput), .SEC_OUTPUT(bigcnt_1_sec_output), .MIN_OUTPUT(bigcnt_1_min_output));
  reg_a reg_a_1 (
    .rega_input(alarma_1_counter_output), .writ(alarma_1_load_register), .reset(in_1), .clk(clock_1_out),
    .rega_output(out_2));
  Binary_to_decimal_converter binary_to_decimal_converter_1 (
    .Bin_num(bigcnt_1_sec_output), .Unit(binary_to_decimal_converter_1_unit),
    .Decimal(binary_to_decimal_converter_1_decimal));
  LED ALARMBUZZ (.in(alarma_1_alarm_sound));
  Binary_to_decimal_converter binary_to_decimal_converter_2 (
    .Bin_num(bigcnt_1_min_output), .Unit(binary_to_decimal_converter_2_unit),
    .Decimal(binary_to_decimal_converter_2_decimal));
  bcd bcd_1 (.number(binary_to_decimal_converter_1_unit), .segment(bcd_1_segment));
  bcd bcd_2 (.number(binary_to_decimal_converter_1_decimal), .segment(bcd_2_segment));
  Binary_to_decimal_converter binary_to_decimal_converter_3 (
    .Bin_num(alarma_1_counter_output), .Unit(binary_to_decimal_converter_3_unit),
    .Decimal(binary_to_decimal_converter_3_decimal));
  _7_Segment_Display u_7_segment_display_1 (
    .g(bcd_1_segment[0]), .f(bcd_1_segment[1]), .a(bcd_1_segment[6]), .b(bcd_1_segment[5]),
    .e(bcd_1_segment[2]), .d(bcd_1_segment[3]), .c(bcd_1_segment[4]));  // open: dp
  _7_Segment_Display u_7_segment_display_2 (
    .g(bcd_2_segment[0]), .f(bcd_2_segment[1]), .a(bcd_2_segment[6]), .b(bcd_2_segment[5]),
    .e(bcd_2_segment[2]), .d(bcd_2_segment[3]), .c(bcd_2_segment[4]));  // open: dp
  bcd bcd_3 (.number(binary_to_decimal_converter_2_unit), .segment(bcd_3_segment));
  bcd bcd_4 (.number(binary_to_decimal_converter_2_decimal), .segment(bcd_4_segment));
  _7_Segment_Display u_7_segment_display_3 (
    .g(bcd_3_segment[0]), .f(bcd_3_segment[1]), .a(bcd_3_segment[6]), .b(bcd_3_segment[5]),
    .e(bcd_3_segment[2]), .d(bcd_3_segment[3]), .c(bcd_3_segment[4]));  // open: dp
  _7_Segment_Display u_7_segment_display_4 (
    .g(bcd_4_segment[0]), .f(bcd_4_segment[1]), .a(bcd_4_segment[6]), .b(bcd_4_segment[5]),
    .e(bcd_4_segment[2]), .d(bcd_4_segment[3]), .c(bcd_4_segment[4]));  // open: dp
  bcd bcd_5 (.number(binary_to_decimal_converter_3_unit), .segment(bcd_5_segment));
  bcd bcd_6 (.number(binary_to_decimal_converter_3_decimal), .segment(bcd_6_segment));
  _7_Segment_Display u_7_segment_display_5 (
    .g(bcd_5_segment[0]), .f(bcd_5_segment[1]), .a(bcd_5_segment[6]), .b(bcd_5_segment[5]),
    .e(bcd_5_segment[2]), .d(bcd_5_segment[3]), .c(bcd_5_segment[4]));  // open: dp
  _7_Segment_Display u_7_segment_display_6 (
    .g(bcd_6_segment[0]), .f(bcd_6_segment[1]), .a(bcd_6_segment[6]), .b(bcd_6_segment[5]),
    .e(bcd_6_segment[2]), .d(bcd_6_segment[3]), .c(bcd_6_segment[4]));  // open: dp
endmodule

module BIGCNT (
  input  CLK,
  input  But,
  input  S,
  input  M,
  input  RES,
  input  EN,
  output ALARMOUTPUT,
  output [7:0] SEC_OUTPUT,
  output [7:0] MIN_OUTPUT
);

  wire minutes_1_borrow, minutes_1_output_hold_seconds, seconds_1_clock_1_min, seconds_1_decrease;

  seconds seconds_1 (
    .clock(CLK), .button(But), .inputfors(S), .borrow(minutes_1_borrow),
    .hold_state(minutes_1_output_hold_seconds), .CU_EN(EN), .reset(RES), .counter_output(SEC_OUTPUT),
    .clock_1_min(seconds_1_clock_1_min), .alarm_output(ALARMOUTPUT), .decrease(seconds_1_decrease));
  minutes minutes_1 (
    .clock(CLK), .button(But), .in_clk(seconds_1_clock_1_min), .decrease(seconds_1_decrease), .inputform(M),
    .ENABLE_FROM_CU(EN), .reset(RES), .counter_output(MIN_OUTPUT), .borrow(minutes_1_borrow),
    .output_hold_seconds(minutes_1_output_hold_seconds));
endmodule

// VHDL entity freq_divider, as the project stores it:
--------------------------------------------------------------------------------
-- Project :
-- File    :
-- Autor   :
-- Date    :
--
--------------------------------------------------------------------------------
-- Description :
--
--------------------------------------------------------------------------------

LIBRARY ieee;
USE ieee.std_logic_1164.all;
USE IEEE.std_logic_UNSIGNED.all;
ENTITY freq_divider IS
  PORT (
  ------------------------------------------------------------------------------
  --Insert input ports below
    clock      : IN  std_logic;                    -- input bit example
    new_clock_1hz : OUT std_logic
    );
END freq_divider;

--------------------------------------------------------------------------------
--Complete your VHDL description below
--------------------------------------------------------------------------------

ARCHITECTURE TypeArchitecture OF freq_divider IS
	
BEGIN
	process(clock)
	variable nr: std_logic_vector(25 downto 0) := (others => '0');
	begin
		if clock'event and clock='1' then
			nr := nr+1;
		end if;
	new_clock_1hz <= nr(25);
	end process;

END TypeArchitecture;

// VHDL entity ONEsec, as the project stores it:
--------------------------------------------------------------------------------
-- Project :
-- File    :
-- Autor   :
-- Date    :
--
--------------------------------------------------------------------------------
-- Description :
--
--------------------------------------------------------------------------------

LIBRARY ieee;
USE ieee.std_logic_1164.all;

use IEEE.STD_LOGIC_UNSIGNED.ALL;
ENTITY ONEsec IS
  PORT (
  clk : in std_logic;
  newclk : out std_logic
    );
END ONEsec;


ARCHITECTURE TypeArchitecture OF ONEsec IS

BEGIN

process (clk)
variable count: std_logic_vector(25 downto 0) := (others => '0');
variable D : std_logic := '0';
begin
if (rising_edge(clk)) then
 if (count = "10111110101111000010000000") then
  count := (others => '0');
  D := not D;
  else
  count := count + '1'; 
 end if;
end if;
newclk <= D;
end process;
END TypeArchitecture;

// VHDL entity alarma, as the project stores it:
--------------------------------------------------------------------------------
-- Project :
-- File    :
-- Autor   :
-- Date    :
--
--------------------------------------------------------------------------------
-- Description :
--
--------------------------------------------------------------------------------

LIBRARY ieee;
USE ieee.std_logic_1164.all;
USE ieee.STD_LOGIC_UNSIGNED.all;
ENTITY alarma IS
  PORT (
  ------------------------------------------------------------------------------
  --Insert input ports below
 	 reload_register :in std_logic_vector(7 downto 0);  
    clock      : IN  std_logic;                    -- input bit example
    button : IN std_logic;
    counter_output : OUT std_logic_vector(7 downto 0);
    set_alarm: IN std_logic;
    alarm_buzz : OUT std_logic;
    alarm_sound : OUT std_logic;
    load_register : OUT std_logic ;
   
    reset : IN std_logic
    );
END alarma;

--------------------------------------------------------------------------------
--Complete your VHDL description below
--------------------------------------------------------------------------------

ARCHITECTURE TypeArchitecture OF alarma IS

signal mode : std_logic := '0' ; -- 1 is up, 0 is down
signal internal_state : std_logic_vector(2 downto 0) := "000"; --00 is up, 01 is hold; 11 is down; 100 is reload reload_register; 101 is new hold before up;
BEGIN
	process(clock, button)
	variable counter : std_logic_vector(7 downto 0):=(others=> '0');
	variable enable : std_logic;
	begin
		if(internal_state = "000") then 
			alarm_buzz <= '0';
		end if;
		if(reset = '1') then
			internal_state <= "000";
			counter := "00000000";
			alarm_buzz <= '0';
			alarm_sound <= '0';
			load_register <= '0';
		else		
		if(button = '1' and internal_state = "000" and set_alarm = '1') then
			load_register <= '0';
			internal_state <= "001";
		elsif(button = '1' and internal_state = "001" and counter > 2) then
			internal_state <= "010";
			load_register <= '1';
		elsif(button = '1' and (internal_state = "101" or internal_state = "010") and set_alarm = '0' ) then
			internal_state <= "011";
			load_register <= '0';
		elsif(internal_state = "100") then
			counter := reload_register;
			internal_state <= "101";
			
		end if;
		alarm_sound <= '0';
		if(rising_edge(clock)) then
		if(internal_state = "001" or internal_state = "011") then enable := '1';
		else enable := '0';
		end if;
		if(enable = '1' and internal_state = "001") then
				counter := counter + 1;
				if counter = "00111100" then
					counter := "00000000";
				end if; 
		elsif(enable = '1' and (internal_state = "011" or internal_state = "101")) then
				alarm_sound <= '1';
				counter := counter - 1;
				if(counter = "00000000") then
					enable := '0';
					internal_state <= "100";
					alarm_buzz <= '1';
				end if;
			end if;
	end if;
	end if;
	counter_output <= counter;
	end process;
	

	
					

END TypeArchitecture;

// VHDL entity seconds, as the project stores it:
--------------------------------------------------------------------------------
-- Project :
-- File    :
-- Autor   :
-- Date    :
--
--------------------------------------------------------------------------------
-- Description :
--
--------------------------------------------------------------------------------

LIBRARY ieee;
USE ieee.std_logic_1164.all;

USE ieee.STD_LOGIC_UNSIGNED.all;
ENTITY seconds IS
  PORT (
  ------------------------------------------------------------------------------
  --Insert input ports below
    clock      : IN  std_logic;                    -- input bit example
    button : IN std_logic;
    counter_output : OUT std_logic_vector(7 downto 0);
    clock_1_min: OUT std_logic;
    inputfors: IN std_logic;
    borrow: in std_logic;
    alarm_output: OUT std_logic;
    decrease : OUT std_logic;
    hold_state : IN std_logic;
    CU_EN : IN std_logic;
    reset : IN std_logic
    
    );
END seconds;

--------------------------------------------------------------------------------
--Complete your VHDL description below
--------------------------------------------------------------------------------

ARCHITECTURE TypeArchitecture OF seconds IS

signal mode : std_logic := '0' ; -- 1 is up, 0 is down
signal internal_state : std_logic_vector(2 downto 0) := "000"; --000 hold, 001 count up, 010 set-up, 011 is hold, 100 is decrease, 101 is HOLD FROM M
BEGIN

	process(clock)
	variable counter : std_logic_vector(7 downto 0):=(others=> '0');
	variable enable : std_logic;
	begin
		alarm_output <= '0';
		if(rising_edge(clock)) then
		clock_1_min <= '0';
		if(reset = '1' or CU_EN = '0') then
			internal_state <= "000";
			counter := "00000000";
			alarm_output <= '0';
		else		
		if(inputfors = '1' and (internal_state = "000" or internal_state = "001" or internal_state = "101" )) then
			internal_state <= "010";
		elsif(inputfors = '1' and internal_state = "010") then
		internal_state <= "011";
		elsif(hold_state = '1') then
		internal_state <= "101";
		end if;
		
		if(button = '1' and internal_state = "000") then
			internal_state <= "001";
		elsif(button = '1' and internal_state = "001" ) then
			internal_state <= "000";
		elsif(button = '1' and internal_state = "011") then
			internal_state <= "100";
		elsif(button = '1' and internal_state = "101") then
			internal_state <= "100";
		end if;
		if(internal_state = "001" or internal_state = "010" or internal_state = "100") then enable := '1';
		else enable := '0';
		end if;
		if(enable = '1' and (internal_state = "001" or internal_state = "010" )) then
				counter := counter + 1;
				if counter = "00111100" then
					clock_1_min <= '1';
					counter := "00000000";
				end if; 
				end if;
		if(enable = '1' and internal_state = "100") then
			if counter = "00000001" then
				clock_1_min <= '1';
				if(borrow = '1') then
					counter := "00111100";
				else 
				internal_state <= "000";
				alarm_output <= '1';
				end if;
			end if;	
			counter := counter - 1;
		end if;
			end if;
	end if;
	decrease <= internal_state(2) and not(internal_state(0));
	counter_output <= counter;
	end process;
	

	
					

END TypeArchitecture;

// VHDL entity minutes, as the project stores it:
--------------------------------------------------------------------------------
-- Project :
-- File    :
-- Autor   :
-- Date    :
--
--------------------------------------------------------------------------------
-- Description :
--
--------------------------------------------------------------------------------

LIBRARY ieee;
USE ieee.std_logic_1164.all;

USE ieee.STD_LOGIC_UNSIGNED.all;
ENTITY minutes IS
  PORT (
  ------------------------------------------------------------------------------
  --Insert input ports below
    clock : IN  std_logic;                    -- input bit example
    button : IN std_logic;
    counter_output : OUT std_logic_vector(7 downto 0);
    in_clk: IN std_logic;
    borrow : OUT std_logic;
    decrease:IN std_logic;
    inputform : IN std_logic;
    ENABLE_FROM_CU : IN std_logic;
    output_hold_seconds: OUT std_logic;
    reset : IN std_logic
    );
END minutes;

--------------------------------------------------------------------------------
--Complete your VHDL description below
--------------------------------------------------------------------------------

ARCHITECTURE TypeArchitecture OF minutes IS

signal mode : std_logic := '0' ; -- 1 is up, 0 is down
signal internal_state : std_logic_vector(2 downto 0) := "000"; --000 is hold, 001 is up, 010 is set-up, 011 is hold, 100 is decrease
BEGIN

	process(clock)
	variable counter : std_logic_vector(7 downto 0):=(others=> '0');
	variable enable : std_logic;
	begin
		if(rising_edge(clock)) then
			output_hold_seconds <= '0';
			if(reset = '1' or ENABLE_FROM_CU = '0') then
			internal_state <= "000";
			counter := "00000000";
			else		
				if(internal_state = "000" and in_clk = '1') then
				internal_state <= "001";
				elsif(decrease = '1') then
				internal_state<= "100";
				elsif((internal_state = "000" or internal_state = "001") and inputform = '1') then
				internal_state <= "010"; 
				output_hold_seconds <= '1';
				elsif(internal_state = "010" and inputform = '1') then
				internal_state <= "100";
				end if;
				if((in_clk = '1' and (internal_state ="000" or internal_state = "001"))or internal_state = "010") then
					counter := counter+1;
					if(counter = "01100100") then
						counter := "00000000";
					end if;
				elsif(in_clk = '1' and internal_state = "100")then 
					if(counter = "00000000") then 
					internal_state <= "000";
					else
					counter := counter - 1;
					end if;
				end if;
			end if;
	end if;
	borrow <= counter(0) or counter(1) or counter(2) or counter(3) or counter(4) or counter(5) or counter(6) or counter(7);
	counter_output <= counter;
	end process;
	

	
					

END TypeArchitecture;

// VHDL entity Binary_to_decimal_converter, as the project stores it:
--------------------------------------------------------------------------------
-- Project :
-- File    :
-- Autor   :
-- Date    :
--
--------------------------------------------------------------------------------
-- Description :
--
--------------------------------------------------------------------------------

LIBRARY ieee;
USE ieee.std_logic_1164.all;
USE ieee.std_logic_unsigned.all;
USE ieee.std_logic_arith.all;

ENTITY Binary_to_decimal_converter IS
  PORT (
 Bin_num: in std_logic_vector(7 downto 0);
  		Unit: out std_logic_vector(3 downto 0);
  		Decimal: out std_logic_vector(3 downto 0)  
    );
END Binary_to_decimal_converter;

--------------------------------------------------------------------------------
--Complete your VHDL description below
--------------------------------------------------------------------------------

ARCHITECTURE comport OF Binary_to_decimal_converter IS

signal num_int: integer:=0;
signal u,z: integer:=0;
BEGIN

	num_int<=conv_integer(bin_num);
	z<=num_int / 10;
	u<=num_int rem 10;
	process(u)
	begin
		case u is
		when 0 => unit <= x"0";
		when 1 => unit <= x"1";
		when 2 => unit <= x"2";
		when 3 => unit <= x"3";
		when 4 => unit <= x"4";
		when 5 => unit <= x"5";
		when 6 => unit <= x"6";
		when 7 => unit <= x"7";
		when 8 => unit <= x"8";
		when 9 => unit <= x"9";
		when others => unit <=x"f";
		end case;
	end process;
	process(z)
	begin
		case z is
		when 0 => Decimal <= x"0";
		when 1 => Decimal <= x"1";
		when 2 => Decimal <= x"2";
		when 3 => Decimal <= x"3";
		when 4 => Decimal <= x"4";
		when 5 => Decimal <= x"5";
		when 6 => Decimal <= x"6";
		when 7 => Decimal <= x"7";
		when 8 => Decimal <= x"8";
		when 9 => Decimal <= x"9";
		when others => Decimal <=x"f";
		end case;
	end process;
		 

	
END comport;

// VHDL entity CommandUnit, as the project stores it:
--------------------------------------------------------------------------------
-- Project : 	MERGE PE PLACUTA IN,LOGISIM NU
-- File    :
-- Autor   :
-- Date    :
--
--------------------------------------------------------------------------------
-- Description :
--
--------------------------------------------------------------------------------

LIBRARY ieee;
USE ieee.std_logic_1164.all;

ENTITY CommandUnit IS
  PORT (
  ------------------------------------------------------------------------------
  --Insert input ports below
    OK_BUT,clk      : IN  std_logic;                    -- input bit example
    START_BUT: IN std_logic;
  	EN_ALARM_UP : OUT std_logic;
  	SET_LED : OUT std_logic;
  	WORKING_TIMER : OUT std_logic;
  	ENABLE_BIGCNT : out std_logic;
  	alarm_input_over : in std_logic;
  	reset : IN std_logic
  	
    );
END CommandUnit;

--------------------------------------------------------------------------------
--Complete your VHDL description below
--------------------------------------------------------------------------------

ARCHITECTURE TypeArchitecture OF CommandUnit IS
type stare is ( Beginning, Idle, ZERO, Ceas_working);
signal stare_act, nxt : stare := Beginning; -- IDLE asteapta setare secunde
BEGIN
	process(clk, reset)
	begin
		if reset = '1' then stare_act<=Beginning;
		else
			if(rising_edge(clk)) then 
				stare_act<=nxt;
			end if;
		end if;
	end process;
	process(stare_act, OK_BUT, START_BUT) --stabilirea starii urmatoare
	begin	
			EN_ALARM_UP <= '0';
			SET_LED <= '0';
			WORKING_TIMER <= '0';
			ENABLE_BIGCNT <= '0';
		case stare_act is
			when Beginning => if START_BUT = '1' then nxt <= Idle;
							else nxt<= Beginning;
						end if;
			when Idle => SET_LED<='1';
					   EN_ALARM_UP <= '1';
					   if OK_BUT = '1' then nxt <= ZERO;
					   else nxt <= Idle;
					   end if;
			when ZERO => SET_LED <= '0';
					   EN_ALARM_UP <= '0';
					   WORKING_TIMER <= '1';
					   if OK_BUT = '1' then nxt <= Ceas_working;
					   else nxt <= ZERO;
					   end if;
			when Ceas_working => ENABLE_bigcnt <= '1';
							WORKING_TIMER <= '1';
			when others => nxt <= Beginning;
					   	   
		end case;
	end process;  

END TypeArchitecture;

// VHDL entity mpg, as the project stores it:
library IEEE;
use IEEE.STD_LOGIC_1164.ALL;
use IEEE.STD_LOGIC_ARITH.ALL; 
use IEEE.STD_LOGIC_UNSIGNED.ALL;

-- Uncomment the following library declaration if using
-- arithmetic functions with Signed or Unsigned values
--use IEEE.NUMERIC_STD.ALL;

-- Uncomment the following library declaration if instantiating
-- any Xilinx leaf cells in this code.
--library UNISIM;
--use UNISIM.VComponents.all;

entity mpg is
  Port ( clk: in STD_LOGIC;
         btn : in STD_LOGIC_VECTOR(4 downto 0); 
         enable : out STD_LOGIC_VECTOR(4 downto 0));
end mpg;

architecture pulsegen of mpg is

signal cnt : STD_LOGIC_VECTOR(15 downto 0);
signal en : STD_LOGIC;
signal q1 : STD_LOGIC_VECTOR(4 downto 0);
signal q2 : STD_LOGIC_VECTOR(4 downto 0);
signal q3 : STD_LOGIC_VECTOR(4 downto 0);

begin

process(clk)
begin
    if clk'event and clk='1' then
         cnt <= cnt + 1;
    end if;
end process;

process(cnt)
begin
    if cnt=x"FFFF" then
        en <= '1';
    else
        en <= '0';
    end if;
end process;

process(clk)
begin
    if clk'event and clk='1' then
        if en = '1' then
            q1 <= btn;
        end if;
    end if;
end process;

process(clk)
begin
    if clk'event and clk='1' then
        q2 <= q1;
    end if;
end process;

process(clk)
begin
    if clk'event and clk='1' then
        q3 <= q2;
    end if;
end process;

enable <= q2 and (not q3);

end pulsegen;

// VHDL entity bcd, as the project stores it:
--------------------------------------------------------------------------------
-- Project :
-- File    :
-- Autor   :
-- Date    :
--
--------------------------------------------------------------------------------
-- Description :
--
--------------------------------------------------------------------------------

LIBRARY ieee;
USE ieee.std_logic_1164.all;

ENTITY bcd IS
  PORT (
  number: in std_logic_vector(3 downto 0);
  segment: out std_logic_vector(6 downto 0)
    );
END bcd;

--------------------------------------------------------------------------------
--Complete your VHDL description below
--------------------------------------------------------------------------------

ARCHITECTURE TypeArchitecture OF bcd IS

signal aux:std_logic_vector (6 downto 0);
BEGIN

with number select
 aux <=
 "1111110" when x"0",
 "0110000" when x"1",
 "1101101" when x"2",
 "1111001" when x"3",
 "0110011" when x"4",
 "1011011" when x"5",
 "1011111" when x"6",
 "1110000" when x"7",
 "1111111" when x"8",
 "1111011" when x"9",
 "0000000" when others;
segment <= aux;

END TypeArchitecture;

// VHDL entity anodss, as the project stores it:
LIBRARY ieee;
USE ieee.std_logic_1164.all;

ENTITY anodss IS
  PORT (
  
    CLK: in std_logic;
    s: out std_logic_vector (6 downto 0);
    AN: out std_logic_vector (7 downto 0);
    segment1, segment2, segment3, segment4, segment5, segment6, segment7, segment8: in std_logic_vector(6 downto 0)
    );
END anodss;

ARCHITECTURE moveanods OF anodss IS

BEGIN
process (CLK)
variable segment:  std_logic_vector (6 downto 0);
variable anozi:  std_logic_vector (7 downto 0);
begin
 if ( CLK = '1') and (CLK'EVENT) then
   case anozi is 
   when "10000000" => anozi := "01000000"; segment := segment2;
   when "01000000" => anozi := "00100000"; segment := segment3;
   when "00100000" => anozi := "00010000"; segment := segment4;
   when "00010000" => anozi := "00001000"; segment := segment5;
   when "00001000" => anozi := "00000100"; segment := segment6;
   when "00000100" => anozi := "00000010"; segment := segment7;
   when "00000010" => anozi := "00000001"; segment := segment8;
   when "00000001" => anozi := "10000000"; segment := segment1;
   when others => anozi := "10000000"; segment := segment1;
   end case;
 end if;
 AN <= anozi;
 s <= Segment;
end process;
END moveanods;

// VHDL entity frequencyDEVIDER, as the project stores it:
LIBRARY ieee;
USE ieee.std_logic_1164.all;
USE ieee.std_logic_UNSIGNED.all;

ENTITY frequencyDEVIDER IS
  PORT (
    CLK, reset : in  std_logic;
    newClock, newclock2   : out std_logic
    );
END frequencyDEVIDER;


ARCHITECTURE devide OF frequencyDEVIDER IS
 
 BEGIN
process (CLK)
   variable counter: std_logic_vector (14 downto 0) := (others => '0');
   variable counter2: std_logic_vector (23 downto 0) := (others => '0');
  begin
   if (CLK = '1') and (CLK'EVENT) then
    if (reset ='1') then
    counter := (others => '0');
    counter2 := (others => '0');
    else
    counter := counter + 1;
    counter2 := counter2 + 1;
    end if;
   end if;
   newClock <= counter (14);
   newClock2 <= counter2 (23);
  end process;
END devide;

// VHDL entity RisingEdge_DFlipFlop, as the project stores it:
-- FPGA projects using VHDL/ VHDL 
-- fpga4student.com
-- VHDL code for D Flip FLop
-- VHDL code for rising edge D flip flop 
Library IEEE;
USE IEEE.Std_logic_1164.all;

entity RisingEdge_DFlipFlop is 
   port(
      Q : out std_logic;    
      Clk :in std_logic;   
      D :in  std_logic    
   );
end RisingEdge_DFlipFlop;
architecture Behavioral of RisingEdge_DFlipFlop is  
begin  
 process(Clk)
 begin 
    if(rising_edge(Clk)) then
   Q <= D; 
    end if;       
 end process;  
 end architecture;

// VHDL entity andGate, as the project stores it:
-- VHDL Code for AND gate

-- Header file declaration

library IEEE;
use IEEE.std_logic_1164.all;

-- Entity declaration

entity andGate is

    port(A : in std_logic;      -- AND gate input
         B : in std_logic;      -- AND gate input
         Y : out std_logic);    -- AND gate output

end andGate;

-- Dataflow Modelling Style
-- Architecture definition

architecture andLogic of andGate is

 begin
    
    Y <= A AND B;

end andLogic;

// VHDL entity reg_a, as the project stores it:
Library IEEE;

use IEEE.std_logic_1164.all;

entity reg_a is

port ( rega_input :in  std_logic_vector(7 downto 0) ;

writ: in std_logic;

reset: in std_logic;

clk: in std_logic;
rega_output: out std_logic_vector(7 downto 0) 

 );

end reg_a;

architecture sim of reg_a is

 begin

process(clk) 

   begin

 if rising_edge(clk) then

if(writ='1') then  

rega_output<=rega_input;

  elsif(reset='1') then

  rega_output<="00000000";     


end if;

      end if;

        end process;

end sim;
